// Logisim project Project1Given.circ as structural Verilog: 5 circuits, main circuit main
module main (
  input  in_1,
  input  in_2,
  input  in_3,
  input  in_4,
  input  Five,
  output N,
  output E,
  output [3:0] out_8
);

  wire fiveseven_1_a, fiveseven_1_b, fiveseven_1_c, fiveseven_1_d, fiveseven_1_e, fiveseven_1_f,
       fiveseven_1_g;

  Compare compare_1 (.X0(1'b1), .Y0(1'b0), .X1(1'b1), .Y1(1'b1), .X2(1'b1), .Y2(1'b1), .N(N), .E(E));
  Gray gray_1 (.B0(1'b1), .B1(1'b0), .B2(1'b1), .B3(1'b1), .G3(out_8[0]), .G2(out_8[1]), .G1(out_8[2]), .G0(out_8[3]));
  FiveSeven fiveseven_1 (
    .V(in_1), .W(in_2), .X(in_3), .Y(in_4), .Z(Five), .A(fiveseven_1_a), .B(fiveseven_1_b),
    .C(fiveseven_1_c), .D(fiveseven_1_d), .E(fiveseven_1_e), .F(fiveseven_1_f), .G(fiveseven_1_g));
  _7_Segment_Display u_7_segment_display_1 (
    .g(fiveseven_1_g), .f(fiveseven_1_f), .a(fiveseven_1_a), .b(fiveseven_1_b), .e(fiveseven_1_e),
    .d(fiveseven_1_d), .c(fiveseven_1_c));  // open: dp
endmodule

module Compare (
  input  X0,
  input  Y0,
  input  X1,
  input  Y1,
  input  X2,
  input  Y2,
  output N,
  output E
);

  wire and_1_out, and_2_out, and_4_out, not_1_out, not_2_out, not_3_out, xnor_1_out, xnor_2_out, xnor_3_out;

  not not_1 (not_1_out, X0);
  not not_2 (not_2_out, X1);
  not not_3 (not_3_out, X2);
  xnor xnor_1 (xnor_1_out, X0, Y0);
  xnor xnor_2 (xnor_2_out, X1, Y1);
  xnor xnor_3 (xnor_3_out, X2, Y2);
  and and_1 (and_1_out, not_1_out, Y0);
  and and_2 (and_2_out, not_2_out, Y1);
  and and_3 (E, xnor_1_out, xnor_2_out, xnor_3_out);
  and and_4 (and_4_out, not_3_out, Y2);
  or or_1 (N, and_1_out, and_2_out, and_4_out);
endmodule

module Gray (
  input  B0,
  input  B1,
  input  B2,
  input  B3,
  output G3,
  output G2,
  output G1,
  output G0
);

  wire AB_out, ACD_out, AnBnCn_out, AnBnDn_out, and_1_out, and_2_out, and_3_out, and_4_out, BCnDn_out,
       BnC_out, BnD_out, not_1_out, not_3_out, not_4_out;

  and ACD (ACD_out, B3, B1, B0);
  not not_1 (not_1_out, B0);
  not not_2 (G0, B1);
  not not_3 (not_3_out, B2);
  not not_4 (not_4_out, B3);
  and AB (AB_out, B3, B2);
  and BnD (BnD_out, not_3_out, B0);
  and BnC (BnC_out, not_3_out, B1);
  and BCnDn (BCnDn_out, B2, G0, not_1_out);
  and and_1 (and_1_out, G0, not_4_out);
  and and_2 (and_2_out, not_3_out, not_4_out);
  and and_3 (and_3_out, not_4_out, not_1_out);
  and AnBnCn (AnBnCn_out, G0, not_3_out, not_4_out);
  and AnBnDn (AnBnDn_out, not_1_out, not_4_out, not_3_out);
  or or_1 (G1, BnD_out, BnC_out, BCnDn_out);
  and and_4 (and_4_out, B0, B3, B2, B1);
  or or_2 (G3, and_4_out, and_1_out, and_2_out, and_3_out);
  or or_3 (G2, AnBnCn_out, AB_out, ACD_out, AnBnDn_out);
endmodule

module FiveSeven (
  input  V,
  input  W,
  input  X,
  input  Y,
  input  Z,
  output A,
  output B,
  output C,
  output D,
  output E,
  output F,
  output G
);

  wire D1_out, eight_out, F1_out, Five_out, Four_out, G1_out, nine_out, not_1_out, not_2_out, not_3_out,
       not_4_out, not_5_out, One_out, Seven_out, Six_out, Three_out, Two_out, V0_out, V1_out, V2_out, V3_out,
       V4_out, zero_out;

  not not_1 (not_1_out, V);
  not not_2 (not_2_out, W);
  not not_3 (not_3_out, X);
  not not_4 (not_4_out, Y);
  not not_5 (not_5_out, Z);
  nor V0 (V0_out, V, W, X, Y);
  ExactlyOne V1 (.out(V1_out), .in0(V), .in1(W), .in2(X), .in3(Y));
  ExactlyOne V3 (.out(V3_out), .in0(not_1_out), .in1(not_2_out), .in2(not_3_out), .in3(not_4_out));
  and V4 (V4_out, V, W, X, Y);
  nor V2 (V2_out, V0_out, V1_out, V3_out, V4_out);
  and zero (zero_out, V0_out, not_5_out);
  and One (One_out, V1_out, not_5_out);
  and Two (Two_out, V2_out, not_5_out);
  and Three (Three_out, V3_out, not_5_out);
  and Four (Four_out, V4_out, not_5_out);
  and Five (Five_out, V0_out, Z);
  and Six (Six_out, V1_out, Z);
  and Seven (Seven_out, V2_out, Z);
  and eight (eight_out, V3_out, Z);
  and nine (nine_out, V4_out, Z);
  or A1 (A, zero_out, Two_out, Three_out, Five_out, Six_out, Seven_out, eight_out, nine_out);
  or B1 (B, zero_out, One_out, Two_out, Three_out, Four_out, Seven_out, eight_out, nine_out);
  not not_6 (C, Two_out);
  ExactlyOne D1 (.out(D1_out), .in0(One_out), .in1(Four_out), .in2(Seven_out));
  or E1 (E, zero_out, Two_out, Six_out, eight_out);
  ExactlyOne F1 (.out(F1_out), .in0(One_out), .in1(Two_out), .in2(Three_out));
  ExactlyOne G1 (.out(G1_out), .in0(zero_out), .in1(Seven_out), .in2(One_out));
  not not_7 (D, D1_out);
  not not_8 (F, F1_out);
  not not_9 (G, G1_out);
  _7_Segment_Display u_7_segment_display_1 (.g(G), .f(F), .a(A), .b(B), .e(E), .d(D), .c(C));  // open: dp
endmodule

module TestFiveSeven (
  input  in_1,
  input  in_2,
  input  in_3,
  input  in_4,
  input  in_5,
  output A,
  output out_7,
  output out_8,
  output out_9,
  output out_10,
  output out_11,
  output out_12
);
endmodule
